// Logisim project NAND Gate.circ as structural Verilog: 1 circuit, main circuit main
module main (
  input  A,
  input  B,
  input  C,
  output out_4
);

  wire A_prime_B_prime_C_out, A_prime_BC_out, A_prime_out, AB_prime_C_out, AB_prime_C_prime_out, ABC_out,
       B_prime_out, C_prime_out;

  nand A_prime (A_prime_out, A, A);
  nand B_prime (B_prime_out, B, B);
  nand C_prime (C_prime_out, C, C);
  nand A_prime_BC (A_prime_BC_out, A_prime_out, B, C);
  nand AB_prime_C_prime (AB_prime_C_prime_out, A, B_prime_out, C_prime_out);
  nand ABC (ABC_out, A, B, C);
  nand AB_prime_C (AB_prime_C_out, A, B_prime_out, C);
  nand A_prime_B_prime_C (A_prime_B_prime_C_out, A_prime_out, B_prime_out, C);
  nand f (out_4, A_prime_B_prime_C_out, A_prime_BC_out, ABC_out, AB_prime_C_out, AB_prime_C_prime_out);
endmodule
